// Logisim project LC3-2200a.circ as structural Verilog
module Datapath (
  input  in_1,
  input  in_2,
  input  in_3,
  input  in_4,
  input  in_5,
  input  in_6,
  input  in_7,
  input  in_8,
  input  [1:0] in_9,
  input  in_10,
  input  in_11,
  input  [3:0] in_12,
  input  in_13,
  input  in_14,
  input  in_15,
  output [3:0] out_16,
  output [3:0] out_17,
  output [3:0] out_18,
  output [3:0] out_19,
  output out_20
);

  wire Clk, n_out, or_1_out, p_out, z_out;
  wire [2:0] comparator_1_gt, register_1_q;
  wire [19:4] IR_q;
  wire [31:0] A_q, alu_1_p3, alu_1_p6, bit_extender_1_out, controlled_buffer_1_out, MAR_q, PC_q, ram_1_data,
       ram_2_data;

  Register #(.width(32)) PC (.D(controlled_buffer_1_out), .en(in_2), .Q(PC_q), .clk(Clk));  // open: clr
  assign controlled_buffer_1_out = in_1 ? PC_q : 32'bz;  // Controlled_Buffer controlled_buffer_1
  Comparator #(.width(32), .mode("unsigned")) comparator_1 (
    .a(controlled_buffer_1_out), .b({32{1'b0}}), .gt(comparator_1_gt[0]), .eq(comparator_1_gt[1]),
    .lt(comparator_1_gt[2]));
  Register #(.width(3)) register_1 (.D(comparator_1_gt), .en(in_15), .Q(register_1_q), .clk(Clk));  // open: clr
  Register #(.width(32)) A (.D(controlled_buffer_1_out), .en(in_5), .Q(A_q), .clk(Clk));  // open: clr
  // ALU alu_1: pin names not known; wires that end beside it: in_9, A_q, alu_1_p3, alu_1_p3, alu_1_p3, alu_1_p6
  assign controlled_buffer_1_out = in_4 ? alu_1_p3 : 32'bz;  // Controlled_Buffer controlled_buffer_2
  Clock clock_1 (.out(Clk));
  Register #(.width(32)) B (.D(controlled_buffer_1_out), .en(in_8), .Q(alu_1_p6), .clk(Clk));  // open: clr
  and p (p_out, register_1_q[0], out_18[0]);
  and z (z_out, register_1_q[1], out_18[1]);
  and n (n_out, register_1_q[2], out_18[2]);
  or or_1 (or_1_out, p_out, z_out);
  or or_2 (out_20, or_1_out, n_out);
  Register #(.width(32)) MAR (.D(controlled_buffer_1_out), .en(in_11), .Q(MAR_q), .clk(Clk));  // open: clr
  RAM #(.addrWidth(4), .dataWidth(32), .bus("separate")) ram_1 (
    .addr(in_12), .din(controlled_buffer_1_out), .data(ram_1_data), .str(in_6), .clk(Clk));  // open: sel, ld, clr
  assign controlled_buffer_1_out = in_7 ? ram_1_data : 32'bz;  // Controlled_Buffer controlled_buffer_3
  Register #(.width(32)) IR (
    .D(controlled_buffer_1_out), .en(in_14), .Q({out_16, out_17, out_18, IR_q, out_19}), .clk(Clk));  // open: clr
  RAM #(.addrWidth(24), .dataWidth(32), .bus("separate")) ram_2 (
    .addr(MAR_q[31:8]), .din(controlled_buffer_1_out), .data(ram_2_data), .str(in_3), .clk(Clk));  // open: sel, ld, clr
  assign controlled_buffer_1_out = in_10 ? ram_2_data : 32'bz;  // Controlled_Buffer controlled_buffer_4
  Bit_Extender #(.in_width(20), .out_width(32), .\type ("input")) bit_extender_1 (
    .in({IR_q, out_19}), .out(bit_extender_1_out));  // open: extend
  assign controlled_buffer_1_out = in_13 ? bit_extender_1_out : 32'bz;  // Controlled_Buffer controlled_buffer_5

  // Other names for the same wires on the sheet: Rz[3:0] = out_19; CC[2:0] = out_18[2:0]; Ry[3:0] = out_18;
  //   Rx[3:0] = out_17; OP[3:0] = out_16; CCMatch = out_20; DrALU = in_4; DrMem = in_10; DrOff = in_13; DrPC = in_1;
  //   DrReg = in_7; Func[1:0] = in_9; LdA = in_5; LdB = in_8; LdCC = in_15; LdIR = in_14; LdMAR = in_11; LdPC = in_2;
  //   Regno[3:0] = in_12; WrMem = in_3; WrReg = in_6
endmodule

module ALU (
  input  [31:0] A,
  input  [31:0] B,
  input  A_2,
  input  D,
  input  [1:0] Func,
  output [31:0] Out
);

  wire [31:0] adder_1_out, adder_2_out, nand_1_out, shifter_1_out, shifter_2_out, shifter_3_out;

  Shifter #(.width(32)) shifter_1 (.in(A), .out(shifter_1_out));  // open: dist
  Shifter #(.width(32), .shift("lr")) shifter_2 (.in(A), .out(shifter_2_out));  // open: dist
  Shifter #(.width(32), .shift("ar")) shifter_3 (.in(A), .out(shifter_3_out));  // open: dist
  Adder #(.width(32)) adder_1 (.a(A), .b(B), .out(adder_1_out));  // open: cin, cout
  assign nand_1_out = ~(A & B);  // NAND_Gate nand_1, 32 bits wide
  Adder #(.width(32)) adder_2 (.a(A), .b(32'h1), .out(adder_2_out));  // open: cin, cout
  Multiplexer #(.select(2), .width(32), .disabled(0), .enable("false")) multiplexer_1 (
    .in0(shifter_1_out), .in1(shifter_2_out), .in2(shifter_1_out), .in3(shifter_3_out), .sel({A_2, D}));  // open: out
  Multiplexer #(.select(2), .width(32), .disabled(0), .enable("false")) multiplexer_2 (
    .in0(adder_1_out), .in1(nand_1_out), .in2(adder_2_out), .out(Out), .sel(Func));  // open: in3
endmodule
